# Fritzing sketch laser-gun-controller (saved by Fritzing 0.9.0b)
breadboards: 1

parts:
  부품1 = Arduino Uno (Rev3)
  LED1 = LED - 5mm [color="Red (633nm)" package="5 mm [THT]"]
  J1 = Basic Servo
  J2 = Basic Servo
  VCC1 = Battery block 9V
  부품2 = Bluetooth Mate Silver

nets:
  N1: 부품1.D9_PWM, J1.pulse
  N2: 부품1.D10_PWM/SS, J2.pulse
  N3: 부품1.D11_PWM/MOSI, LED1.anode
  N4: 부품1.D0/RX, 부품2.TX_5V
  N5: 부품1.D1/TX, 부품2.RX_5V
  5V: 부품1.5V, 부품2.VCC
  GND: 부품1.GND, LED1.cathode, J1.gnd, J2.gnd, VCC1.-, 부품2.GND
  N6: J2.vcc, VCC1.+
